// Logisim project ttl-cpu.circ as structural Verilog: 11 circuits, main circuit main
module main (
);

  wire Clk, MemWrite, or_1_out, PCInc, PCW, stateforop_1_uncond, TBusEn, tdec_1_r1c, tdec_1_r2c, tdec_1_r3c,
       tdec_1_r4c, tdec_1_spc;
  wire [1:0] AddrBusSel, DataBusSel;
  wire [2:0] TSel;
  wire [3:0] LSel, multiplexer_2_out, multiplexer_3_out, NextState, register_1_q, RSel, State,
       stateforop_1_firststate;
  wire [4:0] OpCode;
  wire [7:0] Addr, AddrBus, DataBus, demultiplexer_1_out2, demultiplexer_1_out3, demultiplexer_2_out0,
       demultiplexer_3_out0, LBus, or_2_out, PC, PCData, R1_out, R2_out, R3_out, R4_out, RBus, SP_out, TBus,
       tdec_1_r1, tdec_1_r2, tdec_1_r3, tdec_1_r4, tdec_1_sp;
  wire [15:0] IR;

  Counter u_PC (.load(PCW), .D(PCData), .count(PCInc), .Q(PC), .clk(Clk));  // open: carry, clr
  memory memory_1 (.Clk(Clk), .DataOut(DataBus), .DataIn(DataBus), .Addr(AddrBus), .Write(MemWrite));
  stateforop stateforop_1 (.OpCode(OpCode), .FirstState(stateforop_1_firststate), .uncond(stateforop_1_uncond));
  or or_1 (or_1_out, stateforop_1_uncond, LBus[0]);
  Demultiplexer #(.select(2), .width(8), .enable("false")) demultiplexer_1 (
    .out1(TBus), .out2(demultiplexer_1_out2), .out3(demultiplexer_1_out3), .in(DataBus), .sel(DataBusSel));  // open: out0
  Multiplexer #(.select(2), .width(8), .enable("false")) multiplexer_1 (
    .in0(PC), .out(AddrBus), .sel(AddrBusSel));  // open: in1, in2, in3
  Multiplexer #(.width(4), .enable("false")) multiplexer_2 (
    .in0(4'b0000), .in1(multiplexer_3_out), .out(multiplexer_2_out), .sel(or_1_out));
  Multiplexer #(.width(4), .enable("false")) multiplexer_3 (
    .in0(4'b0001), .in1(stateforop_1_firststate), .out(multiplexer_3_out), .sel(PC[0]));
  assign or_2_out = demultiplexer_1_out2 | demultiplexer_1_out3;  // OR_Gate or_2, 8 bits wide
  Register #(.width(4), .trigger("falling")) register_1 (
    .D(NextState), .en(1'b1), .Q(register_1_q), .clk(Clk));  // open: clr
  reg16 u_IR (.Data(or_2_out), .Write(DataBusSel[1]), .High(DataBusSel[0]), .Clk(Clk), .Output(IR));
  Register #(.width(4)) register_2 (.D(register_1_q), .en(1'b1), .Q(State), .clk(Clk));  // open: clr
  Multiplexer #(.select(4), .width(4), .enable("false")) multiplexer_4 (
    .in0(4'b0010), .in1(4'b0010), .in2(multiplexer_2_out), .in3(4'b0000), .in4(4'b0000), .in5(4'b0000),
    .in6(4'b0000), .in7(4'b0000), .in8(4'b0000), .in9(4'b0000), .in10(4'b0000), .in11(4'b0000),
    .in12(4'b0000), .in13(4'b0000), .in14(4'b0000), .in15(4'b0000), .out(NextState), .sel(State));
  Demultiplexer #(.width(8), .enable("false")) demultiplexer_2 (
    .out0(demultiplexer_2_out0), .in(LBus), .sel(1'b0));  // open: out1
  Demultiplexer #(.width(8), .enable("false")) demultiplexer_3 (
    .out0(demultiplexer_3_out0), .in(RBus), .sel(1'b0));  // open: out1
  state state_1 (
    .State(State), .AddrBusIn(AddrBusSel), .DataBusOut(DataBusSel), .mw(MemWrite), .pcw(PCW), .tb(TBusEn),
    .pci(PCInc));
  LRDec L (.Val(LBus), .Sel(LSel), .PC(PC), .R1(R1_out), .R2(R2_out), .R3(R3_out), .R4(R4_out), .SP(SP_out));
  LRDec lrdec_1 (.Val(RBus), .Sel(RSel), .PC(PC), .R1(R1_out), .R2(R2_out), .R3(R3_out), .R4(R4_out), .SP(SP_out));
  InstrDec instrdec_1 (.In(IR), .OpCode(OpCode), .Addr(Addr), .RSel(LSel), .LSel(RSel), .TSel(TSel));
  ALU alu_1 (.L(demultiplexer_2_out0), .R(demultiplexer_3_out0), .OpCode(OpCode), .T(TBus));  // open: CIn, EQ, LT
  \reg  R1 (.Out(R1_out), .In(tdec_1_r1), .Clk(tdec_1_r1c));
  \reg  R2 (.Out(R2_out), .In(tdec_1_r2), .Clk(tdec_1_r2c));
  \reg  R3 (.Out(R3_out), .In(tdec_1_r3), .Clk(tdec_1_r3c));
  \reg  R4 (.Out(R4_out), .In(tdec_1_r4), .Clk(tdec_1_r4c));
  \reg  SP (.Out(SP_out), .In(tdec_1_sp), .Clk(tdec_1_spc));
  TDec tdec_1 (
    .R1(tdec_1_r1), .R1C(tdec_1_r1c), .R2(tdec_1_r2), .R2C(tdec_1_r2c), .R3(tdec_1_r3), .R3C(tdec_1_r3c),
    .R4(tdec_1_r4), .R4C(tdec_1_r4c), .SP(tdec_1_sp), .SPC(tdec_1_spc), .TSel(TSel), .PC(PCData), .PCW(PCW),
    .Clk(Clk), .Val(TBus));
  Clock u_CLK (.out(Clk));
  // Probe on PC
  // Probe on State
  // Probe on NextState
  // Probe on IR
  // Probe on OpCode
  // Probe on Addr
  // Probe on LSel
  // Probe on LBus
  // Probe on RSel
  // Probe on RBus
  // Probe on TSel
  // Probe on TBus
  // Probe on AddrBus
  // Probe on DataBus

  // Other names for the same wires on the sheet: PCOdd = PC[0]
endmodule

module PC (
  input  CLK,
  input  En,
  output [7:0] Out
);

  wire and_1_out, and_2_out, and_3_out, and_4_out, and_5_out, and_6_out, and_7_out;
  wire [7:0] j_k_ff_1_q;

  and and_1 (and_1_out, En, j_k_ff_1_q[0]);
  and and_2 (and_2_out, En, j_k_ff_1_q[1]);
  and and_3 (and_3_out, En, j_k_ff_1_q[2]);
  and and_4 (and_4_out, En, j_k_ff_1_q[3]);
  and and_5 (and_5_out, En, j_k_ff_1_q[4]);
  and and_6 (and_6_out, En, j_k_ff_1_q[5]);
  and and_7 (and_7_out, En, j_k_ff_1_q[6]);
  // Probe on CLK
  J_K_Flip_Flop j_k_ff_1 (.J(En), .clk(CLK), .K(En), .Q(j_k_ff_1_q[0]));  // open: Qn, preset, en, reset
  J_K_Flip_Flop j_k_ff_2 (.J(En), .clk(and_1_out), .K(En), .Q(j_k_ff_1_q[1]));  // open: Qn, preset, en, reset
  J_K_Flip_Flop j_k_ff_3 (.J(En), .clk(and_2_out), .K(En), .Q(j_k_ff_1_q[2]));  // open: Qn, preset, en, reset
  J_K_Flip_Flop j_k_ff_4 (.J(En), .clk(and_3_out), .K(En), .Q(j_k_ff_1_q[3]));  // open: Qn, preset, en, reset
  J_K_Flip_Flop j_k_ff_5 (.J(En), .clk(and_4_out), .K(En), .Q(j_k_ff_1_q[4]));  // open: Qn, preset, en, reset
  J_K_Flip_Flop j_k_ff_6 (.J(En), .clk(and_5_out), .K(En), .Q(j_k_ff_1_q[5]));  // open: Qn, preset, en, reset
  J_K_Flip_Flop j_k_ff_7 (.J(En), .clk(and_6_out), .K(En), .Q(j_k_ff_1_q[6]));  // open: Qn, preset, en, reset
  J_K_Flip_Flop j_k_ff_8 (.J(En), .clk(and_7_out), .K(En), .Q(j_k_ff_1_q[7]));  // open: Qn, preset, en, reset
  assign Out = ~j_k_ff_1_q;  // NOT_Gate not_1, 8 bits wide
  Counter counter_1 ();  // open: load, D, count, Q, carry, clk, clr
endmodule

module ALU (
  input  [7:0] L,
  input  [7:0] R,
  input  [4:0] OpCode,
  input  CIn,
  output [7:0] T,
  output EQ,
  output LT
);

  wire and_1_out;
  wire [7:0] adder_1_out;

  Adder adder_1 (.a(L), .b(R), .out(adder_1_out), .cin(and_1_out));  // open: cout
  Multiplexer #(.select(4), .width(8)) multiplexer_1 (
    .in0(adder_1_out), .out(T), .sel(OpCode[3:0]), .en(OpCode[4]));  // open: in1, in2, in3, in4, in5, in6, in7, in8, in9, in10, in11, in12, in13, in14, in15
  Comparator comparator_1 (.a(T), .b({8{1'b0}}), .eq(EQ), .lt(LT));  // open: gt
  // Probe on OpCode[0]
  and and_1 (and_1_out, CIn, OpCode[0]);

  // Notes on the sheet:
  //   TODO: Other Ops
  //   TODO: Carry Out
endmodule

// IDec
module InstrDec (
  input  [15:0] In,
  output [7:0] Addr,
  output [3:0] RSel,
  output [3:0] LSel,
  output [2:0] TSel,
  output [4:0] OpCode
);


  assign Addr = In[7:0];
  assign LSel = In[7:4];
  assign OpCode = In[15:11];
  assign RSel = In[3:0];
  assign TSel = In[10:8];
endmodule

// Mem
module memory (
  input  [7:0] DataIn,
  input  Write,
  input  Clk,
  input  [7:0] Addr,
  output [7:0] DataOut
);

  wire controlled_inverter_1_out, decoder_1_out0, decoder_1_out1, decoder_2_out0, decoder_2_out1;
  wire [7:0] rom_1_data;

  Decoder decoder_1 (.out0(decoder_1_out0), .out1(decoder_1_out1), .sel(Addr[7]), .en(1'b1));
  ROM #(.addrWidth(7)) rom_1 (.addr(Addr[6:0]), .data(rom_1_data), .sel(decoder_1_out0));
  // Probe on rom_1_data
  assign DataOut = decoder_2_out0 ? rom_1_data : 8'bz;  // Controlled_Buffer controlled_buffer_1
  assign rom_1_data = decoder_2_out1 ? DataIn : 8'bz;  // Controlled_Buffer controlled_buffer_2
  assign controlled_inverter_1_out = Write ? ~decoder_1_out1 : 1'bz;  // Controlled_Inverter controlled_inverter_1
  RAM #(.addrWidth(7)) ram_1 (
    .addr(Addr[6:0]), .data(rom_1_data), .sel(decoder_1_out1), .clk(Clk), .ld(controlled_inverter_1_out));  // open: clr
  Pull_Resistor pull_resistor_1 (.node(Write));
  Decoder decoder_2 (.out0(decoder_2_out0), .out1(decoder_2_out1), .sel(Write), .en(1'b1));

  // Notes on the sheet:
  //   contents of rom_1 (hex, n*v repeats v):
  //   31 8 32 9 83 12 48 6 1 2
  //   (hackery since Logisim doesn't support bidirectional pins)
endmodule

// Reg
module \reg  (
  input  [7:0] In,
  input  Clk,
  output [7:0] Out
);

  Register #(.trigger("falling")) register_1 (.D(In), .Q(Out), .clk(Clk));  // open: en, clr
endmodule

module LRDec (
  input  [3:0] Sel,
  input  [7:0] R1,
  input  [7:0] R2,
  input  [7:0] R3,
  input  [7:0] R4,
  input  [7:0] SP,
  input  [7:0] PC,
  output [7:0] Val
);

  wire not_1_out;
  wire [7:0] Immed, Reg;

  Multiplexer #(.width(8), .enable("false")) multiplexer_1 (.in0(Reg), .in1(Immed), .out(Val), .sel(Sel[3]));
  not not_1 (not_1_out, Sel[3]);
  Multiplexer #(.select(3), .width(8)) multiplexer_2 (
    .in0(PC), .in1(R1), .in2(R2), .in3(R3), .in4(R4), .in7(SP), .out(Reg), .sel(Sel[2:0]), .en(not_1_out));  // open: in5, in6
  assign Immed = {{5{Sel[2]}}, Sel[2:0]};  // Bit_Extender bit_extender_1
  // Probe on Sel[3]
  // Probe on Immed
  // Probe on Reg
  // Probe on Val

  // Other names for the same wires on the sheet: Result[7:0] = Val; IsImmed = Sel[3]
endmodule

module TDec (
  input  [2:0] TSel,
  input  [7:0] Val,
  input  Clk,
  output [7:0] R1,
  output R1C,
  output [7:0] R2,
  output R2C,
  output [7:0] R3,
  output R3C,
  output [7:0] R4,
  output R4C,
  output [7:0] SP,
  output SPC,
  output [7:0] PC,
  output PCW
);

  Pull_Resistor pull_resistor_1 (.node(R3C));
  Pull_Resistor pull_resistor_2 (.node(SPC));
  Pull_Resistor pull_resistor_3 (.node(R4C));
  Demultiplexer #(.select(3), .width(8), .enable("false")) demultiplexer_1 (
    .out0(PC), .out1(R1), .out2(R2), .out3(R3), .out4(R4), .out7(SP), .in(Val), .sel(TSel));  // open: out5, out6
  Pull_Resistor pull_resistor_4 (.node(R2C));
  Pull_Resistor pull_resistor_5 (.node(PCW));
  Pull_Resistor pull_resistor_6 (.node(R1C));
  // Probe on TSel
  Demultiplexer #(.select(3), .tristate("true"), .disabled(0), .enable("false")) demultiplexer_2 (
    .out0(PCW), .out1(R1C), .out2(R2C), .out3(R3C), .out4(R4C), .out7(SPC), .in(Clk), .sel(TSel));  // open: out5, out6
endmodule

module state (
  input  [3:0] State,
  output [1:0] AddrBusIn,
  output [1:0] DataBusOut,
  output mw,
  output pcw,
  output tb,
  output pci
);

  wire and_2_out, and_3_out, and_4_out, and_5_out, and_6_out, and_8_out, and_10_out, and_11_out, not_1_out,
       not_2_out, not_3_out, not_4_out, not_5_out, not_6_out, not_7_out, not_8_out, not_9_out, not_10_out;

  and and_1 (AddrBusIn[1], State[2], State[1]);
  or or_1 (AddrBusIn[0], State[2], State[3]);
  not not_1 (not_1_out, State[3]);
  not not_2 (not_2_out, State[2]);
  not not_3 (not_3_out, State[3]);
  not not_4 (not_4_out, State[2]);
  not not_5 (not_5_out, State[1]);
  not not_6 (not_6_out, State[0]);
  not not_7 (not_7_out, State[0]);
  and and_2 (and_2_out, State[1], State[0]);
  and and_3 (and_3_out, State[2], State[0]);
  not not_8 (not_8_out, State[2]);
  and and_4 (and_4_out, not_1_out, not_2_out);
  not not_9 (not_9_out, State[1]);
  and and_5 (and_5_out, not_3_out, not_4_out);
  and and_6 (and_6_out, not_5_out, not_6_out);
  and and_7 (mw, State[2], not_7_out);
  or or_2 (tb, and_2_out, and_3_out);
  and and_8 (and_8_out, not_8_out, State[1]);
  not not_10 (not_10_out, State[0]);
  and and_9 (DataBusOut[1], and_4_out, not_9_out);
  and and_10 (and_10_out, and_5_out, and_6_out);
  or or_3 (DataBusOut[0], and_10_out, and_11_out);
  and and_11 (and_11_out, State[2], State[0]);
  and and_12 (pci, and_8_out, not_10_out);

  assign pcw = State[3];
endmodule

// R16
module reg16 (
  input  [7:0] Data,
  input  Clk,
  input  Write,
  input  High,
  output [15:0] Output
);

  wire decoder_1_out0, decoder_1_out1;
  wire [7:0] demultiplexer_1_out0, demultiplexer_1_out1;

  Demultiplexer #(.width(8)) demultiplexer_1 (
    .out0(demultiplexer_1_out0), .out1(demultiplexer_1_out1), .in(Data), .sel(High), .en(Write));
  Decoder decoder_1 (.out0(decoder_1_out0), .out1(decoder_1_out1), .sel(High), .en(Write));
  Register #(.trigger("falling")) H (
    .D(demultiplexer_1_out1), .en(decoder_1_out1), .Q(Output[15:8]), .clk(Clk));  // open: clr
  Register #(.trigger("falling")) L (
    .D(demultiplexer_1_out0), .en(decoder_1_out0), .Q(Output[7:0]), .clk(Clk));  // open: clr
  // Probe on Output[15:8]
  // Probe on Output[7:0]
endmodule

// SFO
module stateforop (
  input  [4:0] OpCode,
  output [3:0] FirstState,
  output uncond
);

  wire and_3_out, not_1_out, not_2_out, not_3_out, not_4_out, not_5_out, not_6_out, or_2_out;

  not not_1 (not_1_out, OpCode[4]);
  not not_2 (not_2_out, OpCode[2]);
  not not_3 (not_3_out, OpCode[4]);
  not not_4 (not_4_out, OpCode[3]);
  not not_5 (not_5_out, OpCode[3]);
  not not_6 (not_6_out, OpCode[3]);
  and and_1 (FirstState[3], not_1_out, not_2_out);
  and and_2 (FirstState[2], not_3_out, not_4_out);
  and and_3 (and_3_out, not_5_out, OpCode[0]);
  or or_1 (FirstState[0], OpCode[1], OpCode[4]);
  or or_2 (or_2_out, not_6_out, OpCode[0]);
  or or_3 (FirstState[1], and_3_out, OpCode[4]);
  or or_4 (uncond, or_2_out, OpCode[4]);
endmodule
